# Fritzing sketch BUS (saved by Fritzing 1.0.1rc)

parts:
  L298N1 = L298N DC motor driver
  A3 = OKY3513
  IR1 = TSOP312.., 314.. [package=THT]  # not connected
  A4 = Wemos S2 Mini [part_number="WeMos D1 Mini Lite"]
  A5 = OKY3513
  A6 = OKY3513

nets:
  N1: L298N1.ENA, A4.Pin_2
  N2: L298N1.ENB, A4.Pin_7
  N3: L298N1.IN1, A4.Pin_3
  N4: L298N1.IN2, A4.Pin_4
  N5: L298N1.IN3, A4.Pin_5
  N6: L298N1.IN4, A4.Pin_6
  N7: A3.Pin_1, A4.Pin_9
  N8: A3.Pin_2, A4.Pin_8, A5.Pin_2, A6.Pin_2
  N9: A3.Pin_3, A4.Pin_18, A4.Pin_26, A5.Pin_3, A6.Pin_3
  N10: A4.Pin_10, A6.Pin_1
  N11: A4.Pin_11, A5.Pin_1

custom parts:
  L298N DC motor driver: 2x DC motor driver with 78M05 positive voltage regulator (7..35 V) L298N: max 46 V, 2 A Set 5 V Enable jumper to enable 5 V regultor (needed for the L298N) and +5 V output at screw terminal or supply external +5 V at screw terminal Set ENA and/or ENB to +5 V to enable motor permanently or supply ENA and/or ENB with PWM signal IN1 and IN2 set rotation directory for motor A (OUT1/OUT2) IN2 and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
  OKY3513: TCRT5000 IR Infrared Sensor Line Tracker Sensor Obstacle Avoidance Module.
  Wemos S2 Mini: A mini wifi board based on the ESP32-S2FN4R2.
